// Logisim project control_device.circ as structural Verilog: 1 circuit, main circuit main
module main (
  input  \Обнулитель 
);

  wire and_1_out, clock_1_out, pull_resistor_1_node, \двигать_шашку_out , \лево_верх_out , \лево_низ_out ,
       \право_верх_out , \прекратить_ход_out ;
  wire [5:0] d_ff_3_q, register_1_q;

  Button \u_лево_верх  (.out(\лево_верх_out ));
  D_Flip_Flop d_ff_1 (.clk(\лево_верх_out ), .D(1'b1), .Q(d_ff_3_q[2]), .reset(and_1_out));  // open: Qn, preset, en
  D_Flip_Flop d_ff_2 (.clk(\лево_низ_out ), .D(1'b1), .Q(d_ff_3_q[4]), .reset(and_1_out));  // open: Qn, preset, en
  Button \u_лево_низ  (.out(\лево_низ_out ));
  and and_1 (and_1_out, 1'b1, \Обнулитель );
  Button \u_двигать_шашку  (.out(\двигать_шашку_out ));
  Button \u_прекратить_ход  (.out(\прекратить_ход_out ));
  D_Flip_Flop d_ff_3 (.clk(\двигать_шашку_out ), .D(1'b1), .Q(d_ff_3_q[0]), .reset(and_1_out));  // open: Qn, preset, en
  Button \u_право_низ  (.out(d_ff_3_q[3]));
  D_Flip_Flop d_ff_4 (
    .clk(\прекратить_ход_out ), .D(1'b1), .Q(d_ff_3_q[5]), .reset(and_1_out));  // open: Qn, preset, en
  Button \u_право_верх  (.out(\право_верх_out ));
  D_Flip_Flop d_ff_5 (.clk(\право_верх_out ), .D(1'b1), .Q(d_ff_3_q[1]), .reset(and_1_out));  // open: Qn, preset, en
  D_Flip_Flop d_ff_6 (.clk(d_ff_3_q[3]), .D(1'b1), .Q(d_ff_3_q[3]), .reset(and_1_out));  // open: Qn, preset, en
  Clock clock_1 (.out(clock_1_out));
  // Probe on register_1_q
  Register #(.width(6)) register_1 (
    .D(d_ff_3_q), .en(1'b1), .Q(register_1_q), .clk(clock_1_out), .clr(pull_resistor_1_node));
  Pull_Resistor pull_resistor_1 (.node(pull_resistor_1_node));
endmodule
